// Logisim project lsc-8.circ as structural Verilog: 31 circuits, main circuit Computer
module Computer (
);

  wire main_1_a_conno, main_1_a_indicate, main_1_a_we, main_1_b_conno, main_1_b_indicate, main_1_b_we,
       main_1_disp_reset, main_1_disp_strobe, main_1_indicate, main_1_kb_reset, main_1_kb_strobe,
       main_1_led_paus, main_1_led_pow, ON_OFF_out, PAUSE_out, RESET_out;
  wire [1:0] n128_kb_removable_storage_ro_1_conno, n128_kb_removable_storage_vol_1_conno;
  wire [6:0] keyboard_1_data, main_1_disp_ascii;
  wire [7:0] main_1_a_dso, main_1_b_dso, n128_kb_removable_storage_ro_1_do,
       n128_kb_removable_storage_vol_1_do;
  wire [16:0] main_1_a_a, main_1_b_a;

  TTY #(.rows(25), .cols(80)) tty_1 (
    .data(main_1_disp_ascii), .clk(main_1_disp_strobe), .clr(main_1_disp_reset));  // open: we
  Button ON_OFF (.out(ON_OFF_out));
  MAIN main_1 (
    .ON_OFF(ON_OFF_out), .PAUSE(PAUSE_out), .RESET(RESET_out), .DISP_ASCII(main_1_disp_ascii),
    .disp_reset(main_1_disp_reset), .DISP_STROBE(main_1_disp_strobe), .LED_POW(main_1_led_pow),
    .LED_PAUS(main_1_led_paus), .KB_ASCII(keyboard_1_data), .KB_STROBE(main_1_kb_strobe),
    .kb_reset(main_1_kb_reset), .A_DSo(main_1_a_dso), .A_DSi(n128_kb_removable_storage_ro_1_do),
    .A_A(main_1_a_a), .A_connO(main_1_a_conno), .A_connI(n128_kb_removable_storage_ro_1_conno),
    .A_WE(main_1_a_we), .B_DSo(main_1_b_dso), .B_DSi(n128_kb_removable_storage_vol_1_do), .B_A(main_1_b_a),
    .B_WE(main_1_b_we), .B_connO(main_1_b_conno), .B_connI(n128_kb_removable_storage_vol_1_conno),
    .A_INDICATE(main_1_a_indicate), .B_INDICATE(main_1_b_indicate), .indicate(main_1_indicate));
  Button PAUSE (.out(PAUSE_out));
  Button RESET (.out(RESET_out));
  LED led_1 (.in(main_1_led_pow));
  LED led_2 (.in(main_1_led_paus));
  Keyboard keyboard_1 (.clk(main_1_kb_strobe), .clr(main_1_kb_reset), .data(keyboard_1_data));  // open: re, avail
  DotMatrix #(.matrixcols(3), .matrixrows(1), .persist(4)) dotmatrix_1 (
    .col0(main_1_indicate), .col1(main_1_a_indicate), .col2(main_1_b_indicate));
  _128_KB_Removable_Storage__RO u_128_kb_removable_storage_ro_1 (
    .A(main_1_a_a), .Di(main_1_a_dso), .WE(main_1_a_we), .connI(main_1_a_conno),
    .Do(n128_kb_removable_storage_ro_1_do), .connO(n128_kb_removable_storage_ro_1_conno));
  _128_KB_Removable_Storage_vol u_128_kb_removable_storage_vol_1 (
    .A(main_1_b_a), .Di(main_1_b_dso), .WE(main_1_b_we), .connI(main_1_b_conno),
    .Do(n128_kb_removable_storage_vol_1_do), .connO(n128_kb_removable_storage_vol_1_conno));
endmodule

module MAIN (
  input  ON_OFF,
  input  PAUSE,
  input  RESET,
  input  [6:0] KB_ASCII,
  input  [7:0] A_DSi,
  input  [1:0] A_connI,
  input  [7:0] B_DSi,
  input  [1:0] B_connI,
  output LED_POW,
  output LED_PAUS,
  output [6:0] DISP_ASCII,
  output DISP_STROBE,
  output disp_reset,
  output [7:0] A_DSo,
  output KB_STROBE,
  output kb_reset,
  output [16:0] A_A,
  output A_WE,
  output A_INDICATE,
  output A_connO,
  output indicate,
  output [7:0] B_DSo,
  output [16:0] B_A,
  output B_WE,
  output B_INDICATE,
  output B_connO
);

  wire clock_state_generator_1_clk, clock_state_generator_1_reset_2, cpu_1_inta, cpu_1_ior, cpu_1_iow,
       cpu_1_memr, cpu_1_memw, interrupt_controller_1_int, ram_rom_select_1_memr_2, ram_rom_select_1_memw_2,
       ram_rom_select_1_romr, storage_controller_1_a_2, storage_controller_1_b, storage_controller_1_c,
       storage_controller_1_d, storage_controller_1_read, storage_controller_1_write;
  wire [7:0] ram_64k_1_do, removable_storage_drive_1_do, removable_storage_drive_1_param,
       storage_controller_1_dw;
  wire [12:0] ram_rom_select_1_roma;
  wire [15:0] cpu_1_a, ram_rom_select_1_rama;
  wire [23:0] storage_controller_1_ao;

  Clock___State_Generator clock_state_generator_1 (
    .RESET_2(clock_state_generator_1_reset_2), .CLK(clock_state_generator_1_clk), .PAUSE_CONTINUE(PAUSE),
    .ON_OFF(ON_OFF), .RESET(RESET), .power(LED_POW), .pause(LED_PAUS));
  RAM_64k ram_64k_1 (
    .A(ram_rom_select_1_rama), .Di(ram_64k_1_do), .Do(ram_64k_1_do), .MEMW(ram_rom_select_1_memw_2),
    .CLK(clock_state_generator_1_clk), .MEMR(ram_rom_select_1_memr_2), .CLR(clock_state_generator_1_reset_2));
  RAM_ROM_Select ram_rom_select_1 (
    .RAMA(ram_rom_select_1_rama), .ROMA(ram_rom_select_1_roma), .A(cpu_1_a), .ROMR(ram_rom_select_1_romr),
    .MEMW(cpu_1_memw), .MEMR(cpu_1_memr), .MEMW_2(ram_rom_select_1_memw_2), .MEMR_2(ram_rom_select_1_memr_2));
  CPU cpu_1 (
    .A(cpu_1_a), .Di(ram_64k_1_do), .Do(ram_64k_1_do), .INTR(interrupt_controller_1_int),
    .CLK(clock_state_generator_1_clk), .RESET(clock_state_generator_1_reset_2), .MEMW(cpu_1_memw),
    .MEMR(cpu_1_memr), .IOW(cpu_1_iow), .IOR(cpu_1_ior), .INTA(cpu_1_inta));  // open: READY
  Interrupt_Controller interrupt_controller_1 (
    .D(ram_64k_1_do), .RESET(clock_state_generator_1_reset_2), .INTA(cpu_1_inta),
    .INT(interrupt_controller_1_int));  // open: IR7, IR6, IR5, IR4, IR3, IR2, IR1, IR0
  ROM_8k rom_8k_1 (.A(ram_rom_select_1_roma), .D(ram_64k_1_do), .CS(ram_rom_select_1_romr));
  VideoCard videocard_1 (
    .Di(ram_64k_1_do), .A(cpu_1_a), .RST(clock_state_generator_1_reset_2), .IOW(cpu_1_iow),
    .ASCII(DISP_ASCII), .reset(disp_reset), .STROBE(DISP_STROBE), .IOR(cpu_1_ior), .Do(ram_64k_1_do),
    .CLK(clock_state_generator_1_clk));
  Keyboard_Controller keyboard_controller_1 (
    .ASCII(KB_ASCII), .A(cpu_1_a), .IOR(cpu_1_ior), .RST(clock_state_generator_1_reset_2), .Do(ram_64k_1_do),
    .STROBE(KB_STROBE), .reset(kb_reset), .Di(ram_64k_1_do), .IOW(cpu_1_iow));
  Storage_Controller storage_controller_1 (
    .Di(ram_64k_1_do), .IOW(cpu_1_iow), .A(cpu_1_a), .IOR(cpu_1_ior), .CLK(clock_state_generator_1_clk),
    .RST(clock_state_generator_1_reset_2), .Do(ram_64k_1_do), .Dw(storage_controller_1_dw),
    .Ao(storage_controller_1_ao), .A_2(storage_controller_1_a_2), .B(storage_controller_1_b),
    .C(storage_controller_1_c), .D(storage_controller_1_d), .param(removable_storage_drive_1_param),
    .Dr(removable_storage_drive_1_do), .READ(storage_controller_1_read), .WRITE(storage_controller_1_write),
    .indicate(indicate));
  Removable_Storage_Drive removable_storage_drive_1 (
    .Di(storage_controller_1_dw), .READ(storage_controller_1_read), .A(storage_controller_1_ao),
    .WRITE(storage_controller_1_write), .sel(storage_controller_1_a_2), .Do(removable_storage_drive_1_do),
    .param(removable_storage_drive_1_param), .DSo(A_DSo), .Ao(A_A), .DSi(A_DSi), .WE(A_WE), .connI(A_connI),
    .connO(A_connO), .indicate(A_INDICATE));
  Removable_Storage_Drive removable_storage_drive_2 (
    .Di(storage_controller_1_dw), .READ(storage_controller_1_read), .A(storage_controller_1_ao),
    .WRITE(storage_controller_1_write), .sel(storage_controller_1_b), .Do(removable_storage_drive_1_do),
    .param(removable_storage_drive_1_param), .DSo(B_DSo), .Ao(B_A), .DSi(B_DSi), .WE(B_WE), .connI(B_connI),
    .connO(B_connO), .indicate(B_INDICATE));
  _16_MB_Storage__RO u_16_mb_storage_ro_1 (
    .A(storage_controller_1_ao), .Do(removable_storage_drive_1_do), .sel(storage_controller_1_c),
    .param(removable_storage_drive_1_param), .Di(storage_controller_1_dw),
    .WRITE(storage_controller_1_write), .READ(storage_controller_1_read));
  _128_KB_Storage__vol u_128_kb_storage_vol_1 (
    .Di(storage_controller_1_dw), .READ(storage_controller_1_read), .A(storage_controller_1_ao),
    .WRITE(storage_controller_1_write), .sel(storage_controller_1_d), .Do(removable_storage_drive_1_do),
    .param(removable_storage_drive_1_param));

  // Notes on the sheet:
  //   B_DSi: pull=down
  //   KB_ASCII: pull=down
  //   B_connI: pull=down
  //   PAUSE: pull=down
  //   RESET: pull=down
  //   A_DSi: pull=down
  //   ON_OFF: pull=down
  //   A_connI: pull=down
endmodule

module CPU (
  input  [7:0] Di,
  input  CLK,
  input  RESET,
  input  INTR,
  input  READY,
  output [7:0] Do,
  output [15:0] A,
  output INTA,
  output MEMW,
  output IOW,
  output MEMR,
  output IOR
);

  wire control_unit_1_alu_flag_read, control_unit_1_alu_oe, control_unit_1_alu_reg_a_b,
       control_unit_1_alu_reg_en, control_unit_1_alu_reg_i_o, control_unit_1_as_pc_l_h,
       control_unit_1_as_pc_oe, control_unit_1_as_pc_pop, control_unit_1_as_pc_push, control_unit_1_as_pc_we,
       control_unit_1_den, control_unit_1_dt_nr, control_unit_1_fr_oe, control_unit_1_fr_we,
       control_unit_1_regs_acc_select, control_unit_1_regs_ao, control_unit_1_regs_re,
       control_unit_1_regs_we, control_unit_1_stack_pop, control_unit_1_stack_push, flag_registers_1_co;
  wire [1:0] control_unit_1_fs;
  wire [2:0] control_unit_1_regs_ddd, control_unit_1_regs_sss;
  wire [3:0] alu_1_fo, control_unit_1_alu_code;
  wire [4:0] flag_registers_1_cnd;
  wire [7:0] alu_1_q;

  ALU alu_1 (
    .D(alu_1_q), .a_b(control_unit_1_alu_reg_a_b), .OE(control_unit_1_alu_oe), .Q(alu_1_q), .CLK(CLK),
    .CF_in(flag_registers_1_co), .FO(alu_1_fo), .RST(RESET), .reg_i_o(control_unit_1_alu_reg_i_o),
    .reg_OE(alu_1_q), .CODE(control_unit_1_alu_code), .FR(control_unit_1_alu_flag_read),
    .reg_EN(control_unit_1_alu_reg_en));
  Flag_Registers flag_registers_1 (
    .PSZC(alu_1_q), .CLK(CLK), .RST(RESET), .O_en(control_unit_1_fr_oe), .FI(alu_1_fo),
    .CO(flag_registers_1_co), .CND(flag_registers_1_cnd), .WE(control_unit_1_fr_we), .Di(alu_1_q),
    .FS(control_unit_1_fs));
  DB_Buffer db_buffer_1 (
    .DI(Di), .DO(Do), .i_o(control_unit_1_dt_nr), .in_4(alu_1_q), .out_6(alu_1_q), .EN(control_unit_1_den));
  Control_Unit control_unit_1 (
    .II(alu_1_q), .CLK(CLK), .RST(RESET), .ALU_REG_EN(control_unit_1_alu_reg_en),
    .ALU_REG_I_O(control_unit_1_alu_reg_i_o), .ALU_Flag_Read(control_unit_1_alu_flag_read),
    .ALU_CODE(control_unit_1_alu_code), .FR_OE(control_unit_1_fr_oe), .REGs_RE(control_unit_1_regs_re),
    .REGs_WE(control_unit_1_regs_we), .REGs_DDD(control_unit_1_regs_ddd), .REGs_SSS(control_unit_1_regs_sss),
    .REGs_AO(control_unit_1_regs_ao), .AS_PC_WE(control_unit_1_as_pc_we), .AS_PC_OE(control_unit_1_as_pc_oe),
    .AS_PC_L_H(control_unit_1_as_pc_l_h), .AS_PC_PUSH(control_unit_1_as_pc_push),
    .AS_PC_POP(control_unit_1_as_pc_pop), .DEN(control_unit_1_den), .DT_nR(control_unit_1_dt_nr),
    .ALU_REG_a_b(control_unit_1_alu_reg_a_b), .ALU_OE(control_unit_1_alu_oe),
    .REGs_Acc_select(control_unit_1_regs_acc_select), .CND(flag_registers_1_cnd), .AO(A),
    .Stack_PUSH(control_unit_1_stack_push), .Stack_POP(control_unit_1_stack_pop), .MEMW(MEMW), .MEMR(MEMR),
    .IOW(IOW), .IOR(IOR), .INTA(INTA), .FR_WE(control_unit_1_fr_we), .INTR(INTR), .FS(control_unit_1_fs));
  Scratch_Pad scratch_pad_1 (
    .D_in(alu_1_q), .reg_in(control_unit_1_regs_ddd), .WE(control_unit_1_regs_we), .D_out(alu_1_q),
    .CLK(CLK), .RST(RESET), .reg_out(control_unit_1_regs_sss), .RE(control_unit_1_regs_re), .A(A),
    .AO(control_unit_1_regs_ao), .AS(control_unit_1_regs_acc_select));
  AS___PC as_pc_1 (
    .PUSH(control_unit_1_as_pc_push), .POP(control_unit_1_as_pc_pop), .D(alu_1_q),
    .L_H(control_unit_1_as_pc_l_h), .WE(control_unit_1_as_pc_we), .OE(control_unit_1_as_pc_oe), .A(A),
    .CLK(CLK), .RST(RESET));
  Data_Stack data_stack_1 (
    .PUSH(control_unit_1_stack_push), .POP(control_unit_1_stack_pop), .OUT(alu_1_q), .CLK(CLK), .RST(RESET),
    .IN(alu_1_q));

  // Notes on the sheet:
  //   RESET: pull=down
  //   INTR: pull=down
  //   READY: pull=down
  //   CLK: pull=down
endmodule

module Scratch_Pad (
  input  CLK,
  input  RST,
  input  [7:0] D_in,
  input  [2:0] reg_in,
  input  WE,
  input  AS,
  input  RE,
  input  [2:0] reg_out,
  input  AO,
  output [7:0] D_out,
  output [15:0] A
);

  wire decoder_1_out0, decoder_1_out1, decoder_1_out2, decoder_1_out3, decoder_1_out4, decoder_1_out5,
       decoder_1_out6, xor_1_out, xor_2_out;
  wire [2:0] controlled_buffer_1_out, controlled_buffer_2_out;
  wire [7:0] A_q, B_q, C_q, D_q, E_q, H_q, L_q;

  assign controlled_buffer_1_out = xor_1_out ? reg_in : 3'bz;  // Controlled_Buffer controlled_buffer_1
  xor xor_1 (xor_1_out, AS, WE);
  xor xor_2 (xor_2_out, AS, RE);
  assign controlled_buffer_2_out = xor_2_out ? reg_out : 3'bz;  // Controlled_Buffer controlled_buffer_2
  Decoder #(.select(3), .disabled(0)) decoder_1 (
    .out0(decoder_1_out0), .out1(decoder_1_out1), .out2(decoder_1_out2), .out3(decoder_1_out3),
    .out4(decoder_1_out4), .out5(decoder_1_out5), .out6(decoder_1_out6), .sel(controlled_buffer_1_out),
    .en(WE));  // open: out7
  Pull_Resistor pull_resistor_1 (.node(controlled_buffer_1_out));
  Pull_Resistor pull_resistor_2 (.node(controlled_buffer_2_out));
  Register #(.trigger("high")) u_A (.D(D_in), .en(decoder_1_out0), .Q(A_q), .clk(CLK), .clr(RST));
  Register #(.trigger("high")) B (.D(D_in), .en(decoder_1_out1), .Q(B_q), .clk(CLK), .clr(RST));
  Register #(.trigger("high")) C (.D(D_in), .en(decoder_1_out2), .Q(C_q), .clk(CLK), .clr(RST));
  Register #(.trigger("high")) D (.D(D_in), .en(decoder_1_out3), .Q(D_q), .clk(CLK), .clr(RST));
  Register #(.trigger("high")) E (.D(D_in), .en(decoder_1_out4), .Q(E_q), .clk(CLK), .clr(RST));
  Register #(.trigger("high")) H (.D(D_in), .en(decoder_1_out5), .Q(H_q), .clk(CLK), .clr(RST));
  Register #(.trigger("high")) L (.D(D_in), .en(decoder_1_out6), .Q(L_q), .clk(CLK), .clr(RST));
  Multiplexer #(.select(3), .width(8)) multiplexer_1 (
    .in0(A_q), .in1(B_q), .in2(C_q), .in3(D_q), .in4(E_q), .in5(H_q), .in6(L_q), .out(D_out),
    .sel(controlled_buffer_2_out), .en(RE));  // open: in7
  assign A = AO ? {H_q, L_q} : 16'bz;  // Controlled_Buffer controlled_buffer_3

  // Notes on the sheet:
  //   CLK: pull=down
  //   reg_in: pull=down
  //   reg_out: pull=down
  //   RE: pull=down
  //   RST: pull=down
  //   AO: pull=down
  //   AS: pull=down
  //   WE: pull=down
endmodule

module ALU (
  input  CLK,
  input  RST,
  input  CF_in,
  input  [7:0] D,
  input  a_b,
  input  reg_i_o,
  input  [3:0] CODE,
  input  reg_EN,
  input  OE,
  input  FR,
  output [7:0] reg_OE,
  output [3:0] FO,
  output [7:0] Q
);

  wire adder_1_cout, and_1_out, and_2_out, and_3_out, and_4_out, and_5_out, and_6_out, and_7_out, d_ff_1_q,
       decoder_1_out0, decoder_1_out1, decoder_2_out0, decoder_2_out1, multiplexer_2_out, multiplexer_4_out,
       multiplexer_5_out, nand_1_out, nand_2_out, nor_1_out, not_1_out, or_2_out, or_3_out, or_4_out,
       shifter_1_carry_o, xor_3_out, xor_4_out;
  wire [3:0] bitadder_1_out, CF_out, decoder_2_out3, xor_1_out;
  wire [7:0] a_q, adder_1_out, and_8_out, b_q, controlled_buffer_2_out, multiplexer_3_out, multiplexer_6_out,
       or_5_out, shifter_1_q, xor_2_out, xor_5_out;
  wire [7:7] or_1_out;

  Decoder #(.disabled(0)) decoder_1 (.out0(decoder_1_out0), .out1(decoder_1_out1), .sel(a_b), .en(and_1_out));
  and and_1 (and_1_out, reg_EN, ~reg_i_o);  // AND_Gate
  and and_2 (and_2_out, reg_EN, reg_i_o);
  Register a (.D(D), .en(decoder_1_out0), .Q(a_q), .clk(CLK), .clr(RST));
  Register b (.D(D), .en(decoder_1_out1), .Q(b_q), .clk(CLK), .clr(RST));
  Multiplexer #(.width(8)) multiplexer_1 (.in0(a_q), .in1(b_q), .out(reg_OE), .sel(a_b), .en(and_2_out));
  D_Flip_Flop d_ff_1 (.clk(CLK), .D(CF_in), .Q(d_ff_1_q));  // open: Qn, preset, en, reset
  or or_1 (or_1_out[7], and_3_out, and_5_out);
  and and_3 (and_3_out, CODE[0], decoder_2_out1, CODE[1]);
  Decoder #(.select(2), .disabled(0), .enable("false")) decoder_2 (
    .out0(decoder_2_out0), .out1(decoder_2_out1), .out2(decoder_2_out3[3]), .out3(decoder_2_out3[0]),
    .sel(CODE[3:2]));
  and and_4 (and_4_out, or_2_out, CODE[0]);
  and and_5 (and_5_out, CODE[1], or_2_out);
  or or_2 (or_2_out, decoder_2_out0, decoder_2_out3[0]);
  nand nand_1 (nand_1_out, decoder_2_out1, CODE[1], CODE[0]);
  Multiplexer #(.disabled(0), .enable("false")) multiplexer_2 (
    .in0(1'b0), .in1(OE), .out(multiplexer_2_out), .sel(nand_1_out));
  // Probe on a_q
  or or_3 (or_3_out, decoder_2_out3[3], decoder_2_out3[0]);
  Multiplexer #(.width(8), .enable("false")) multiplexer_3 (
    .in0(b_q), .in1(8'h1), .out(multiplexer_3_out), .sel(or_3_out));
  // Probe on multiplexer_3_out
  and and_6 (and_6_out, CODE[1], CODE[0]);
  assign xor_1_out = {{3{decoder_2_out3[3]}}, decoder_2_out3[0]} ^ 4'b1111;  // XOR_Gate xor_1, 4 bits wide
  assign xor_2_out = {8{or_1_out[7]}} ^ multiplexer_3_out;  // XOR_Gate xor_2, 8 bits wide
  xor xor_3 (xor_3_out, or_1_out[7], adder_1_cout);
  Multiplexer #(.enable("false")) multiplexer_4 (
    .in0(xor_3_out), .in1(shifter_1_carry_o), .out(multiplexer_4_out), .sel(decoder_2_out3[3]));
  nand nand_2 (nand_2_out, ~and_6_out, decoder_2_out1, ~decoder_2_out3[3]);  // NAND_Gate
  Multiplexer #(.enable("false")) multiplexer_5 (
    .in0(1'b0), .in1(multiplexer_4_out), .out(multiplexer_5_out), .sel(nand_2_out));
  assign CF_out[0] = xor_1_out[0] ? multiplexer_5_out : 1'bz;  // Controlled_Buffer CF
  // Probe on xor_2_out
  nor nor_1 (nor_1_out, bitadder_1_out[3], bitadder_1_out[2], bitadder_1_out[1], bitadder_1_out[0]);
  assign CF_out[1] = xor_1_out[1] ? nor_1_out : 1'bz;  // Controlled_Buffer ZF
  assign FO = FR ? CF_out : 4'bz;  // Controlled_Buffer controlled_buffer_1
  and and_7 (and_7_out, and_4_out, d_ff_1_q);
  xor xor_4 (xor_4_out, or_1_out[7], and_7_out);
  Adder adder_1 (.a(a_q), .b(xor_2_out), .out(adder_1_out), .cin(xor_4_out), .cout(adder_1_cout));
  or or_4 (or_4_out, decoder_2_out3[0], decoder_2_out0);
  assign controlled_buffer_2_out = or_4_out ? adder_1_out : 8'bz;  // Controlled_Buffer controlled_buffer_2
  not not_1 (not_1_out, bitadder_1_out[0]);
  assign CF_out[2] = xor_1_out[2] ? controlled_buffer_2_out[7] : 1'bz;  // Controlled_Buffer SF
  assign CF_out[3] = xor_1_out[3] ? not_1_out : 1'bz;  // Controlled_Buffer PF
  assign and_8_out = a_q & xor_2_out;  // AND_Gate and_8, 8 bits wide
  Multiplexer #(.select(2), .width(8)) multiplexer_6 (
    .in0(and_8_out), .in1(xor_5_out), .in2(or_5_out), .in3(adder_1_out), .out(multiplexer_6_out),
    .sel(CODE[1:0]), .en(decoder_2_out1));
  Multiplexer #(.width(8), .enable("false")) multiplexer_7 (
    .in0(multiplexer_6_out), .in1(shifter_1_q), .out(controlled_buffer_2_out), .sel(decoder_2_out3[3]));
  // Probe on controlled_buffer_2_out
  assign Q = multiplexer_2_out ? controlled_buffer_2_out : 8'bz;  // Controlled_Buffer controlled_buffer_3
  // Probe on Q
  assign xor_5_out = a_q ^ xor_2_out;  // XOR_Gate xor_5, 8 bits wide
  BitAdder bitadder_1 (.in0(controlled_buffer_2_out), .out(bitadder_1_out));
  assign or_5_out = a_q | xor_2_out;  // OR_Gate or_5, 8 bits wide
  shifter shifter_1 (
    .a(a_q), .b(xor_2_out), .mode(CODE[1:0]), .carry(and_7_out), .carry_o(shifter_1_carry_o), .q(shifter_1_q));

  // Notes on the sheet:
  //   CF_in: pull=down
  //   OE: pull=down
  //   reg_i_o: pull=down
  //   RST: pull=down
  //   CLK: pull=down
  //   a_b: pull=down
  //   FR: pull=down
  //   CODE: pull=down
  //   reg_EN: pull=down
endmodule

module shifter (
  input  carry,
  input  [7:0] a,
  input  [7:0] b,
  input  [1:0] mode,
  output carry_o,
  output [7:0] q
);

  wire [7:0] shifter_1_out, shifter_2_out, shifter_3_out, shifter_4_out;

  Shifter #(.shift("rl")) shifter_1 (.in(a), .\dist (b[2:0]), .out(shifter_1_out));
  Multiplexer #(.select(2), .enable("false")) multiplexer_1 (
    .in0(a[7]), .in1(a[0]), .in2(a[7]), .in3(a[0]), .out(carry_o), .sel(mode));
  Shifter #(.shift("rr")) shifter_2 (.in(a), .\dist (b[2:0]), .out(shifter_2_out));
  Shifter shifter_3 (.in(a), .\dist (b[2:0]), .out(shifter_3_out));
  Shifter #(.shift("lr")) shifter_4 (.in(a), .\dist (b[2:0]), .out(shifter_4_out));
  Multiplexer #(.select(2), .width(8), .enable("false")) multiplexer_2 (
    .in0(shifter_1_out), .in1(shifter_2_out), .in2({shifter_3_out[7:1], carry}),
    .in3({carry, shifter_4_out[6:0]}), .out(q), .sel(mode));
endmodule

module Flag_Registers (
  input  WE,
  input  O_en,
  input  CLK,
  input  RST,
  input  [3:0] FI,
  input  [7:0] Di,
  input  [1:0] FS,
  output CO,
  output [7:0] PSZC,
  output [4:0] CND
);

  wire and_1_out, decoder_1_out1, decoder_1_out2, decoder_1_out3, decoder_2_out0, decoder_2_out1,
       decoder_2_out2, decoder_2_out3, or_1_out, or_2_out, or_3_out;
  wire [7:4] controlled_buffer_1_out;
  wire [7:7] pull_resistor_1_node;

  assign {controlled_buffer_1_out, FI} = decoder_1_out1 ? Di : 8'bz;  // Controlled_Buffer controlled_buffer_1
  Decoder #(.select(2), .disabled(0), .enable("false")) decoder_1 (
    .out1(decoder_1_out1), .out2(decoder_1_out2), .out3(decoder_1_out3), .sel({O_en, WE}));  // open: out0
  and and_1 (and_1_out, ~decoder_1_out3, CLK);  // AND_Gate
  or or_1 (or_1_out, decoder_1_out1, and_1_out);
  or or_2 (or_2_out, decoder_2_out3, RST);
  Decoder #(.select(2), .disabled(0)) decoder_2 (
    .out0(decoder_2_out0), .out1(decoder_2_out1), .out2(decoder_2_out2), .out3(decoder_2_out3), .sel(FS),
    .en(decoder_1_out3));
  D_Flip_Flop Carry (
    .clk(or_1_out), .D(FI[0]), .Q(CND[0]), .preset(decoder_2_out1), .en(or_1_out), .reset(or_3_out));  // open: Qn
  or or_3 (or_3_out, decoder_2_out0, RST);
  D_Flip_Flop Zero (.clk(or_1_out), .D(FI[1]), .Q(CND[1]), .en(or_1_out), .reset(RST));  // open: Qn, preset
  D_Flip_Flop Sign (.clk(or_1_out), .D(FI[2]), .Q(CND[2]), .en(or_1_out), .reset(RST));  // open: Qn, preset
  D_Flip_Flop Parity (.clk(or_1_out), .D(FI[3]), .Q(CND[3]), .en(or_1_out), .reset(RST));  // open: Qn, preset
  D_Flip_Flop Interrupt (
    .clk(or_1_out), .D(controlled_buffer_1_out[4]), .Q(CND[4]), .preset(or_2_out), .en(decoder_1_out1),
    .reset(decoder_2_out2));  // open: Qn
  Pull_Resistor pull_resistor_1 (.node(pull_resistor_1_node[7]));
  assign PSZC = decoder_1_out2 ? {{3{pull_resistor_1_node[7]}}, CND} : 8'bz;  // Controlled_Buffer controlled_buffer_2

  assign CO = CND[0];

  // Notes on the sheet:
  //   FS: pull=down
  //   O_en: pull=down
  //   Di: pull=down
  //   CLK: pull=down
  //   RST: pull=down
  //   WE: pull=down
endmodule

module DB_Buffer (
  input  [7:0] DI,
  input  i_o,
  input  EN,
  input  [7:0] in_4,
  output [7:0] DO,
  output [7:0] out_6
);

  wire and_1_out, and_2_out;

  assign out_6 = and_2_out ? DI : 8'bz;  // Controlled_Buffer controlled_buffer_1
  assign DO = and_1_out ? in_4 : 8'bz;  // Controlled_Buffer controlled_buffer_2
  and and_1 (and_1_out, i_o, EN);
  and and_2 (and_2_out, ~i_o, EN);  // AND_Gate

  // Notes on the sheet:
  //   EN: pull=down
  //   i_o: pull=down
endmodule

module Clock___State_Generator (
  input  PAUSE_CONTINUE,
  input  ON_OFF,
  input  RESET,
  output CLK,
  output RESET_2,
  output pause,
  output power
);

  wire clock_1_out, or_1_out, t_ff_1_qn, t_ff_2_qn, xor_1_out;

  buf xor_1 (xor_1_out, clock_1_out);  // XOR_Gate
  Clock clock_1 (.out(clock_1_out));
  delayer_25 delayer_25_1 ();  // open: in, out
  T_Flip_Flop t_ff_1 (
    .clk(PAUSE_CONTINUE), .T(PAUSE_CONTINUE), .Q(pause), .Qn(t_ff_1_qn), .reset(or_1_out));  // open: preset, en
  T_Flip_Flop t_ff_2 (.clk(ON_OFF), .T(ON_OFF), .Q(power), .Qn(t_ff_2_qn));  // open: preset, reset, en
  Pull_Resistor pull_resistor_1 (.node(CLK));
  assign CLK = t_ff_1_qn ? xor_1_out : 1'bz;  // Controlled_Buffer controlled_buffer_1
  or or_1 (or_1_out, t_ff_2_qn, RESET);
  D_Flip_Flop #(.trigger("falling")) d_ff_1 (
    .clk(CLK), .D(power), .Qn(RESET_2), .reset(or_1_out));  // open: Q, preset, en

  // Notes on the sheet:
  //   PAUSE_CONTINUE: pull=down
  //   ON_OFF: pull=down
  //   RESET: pull=down
endmodule

module AS___PC (
  input  CLK,
  input  RST,
  input  PUSH,
  input  POP,
  input  [7:0] D,
  input  L_H,
  input  WE,
  input  OE,
  output [15:0] A
);

  wire and_1_out, buffer_1_out, buffer_2_out, decoder_1_out0, decoder_1_out1, multiplexer_2_out, not_1_out,
       or_1_out, or_2_out, or_3_out;
  wire [7:0] counter_1_q, H_q, L_q, multiplexer_1_out;
  wire [15:0] counter_2_q, multiplexer_3_out, ram_1_data;

  or or_1 (or_1_out, PUSH, POP);
  Decoder #(.disabled(0)) decoder_1 (.out0(decoder_1_out0), .out1(decoder_1_out1), .sel(L_H), .en(WE));
  not not_1 (not_1_out, CLK);
  Multiplexer #(.width(8), .disabled(0), .enable("false")) multiplexer_1 (
    .in0(D), .in1(8'he0), .out(multiplexer_1_out), .sel(RST));
  Counter counter_1 (
    .load(POP), .count(or_1_out), .Q(counter_1_q), .clk(multiplexer_2_out), .clr(RST));  // open: D, carry
  Multiplexer #(.disabled(0), .enable("false")) multiplexer_2 (
    .in0(not_1_out), .in1(CLK), .out(multiplexer_2_out), .sel(POP));
  Register L (.D(D), .en(decoder_1_out0), .Q(L_q), .clk(CLK), .clr(RST));
  Register H (.D(multiplexer_1_out), .en(or_2_out), .Q(H_q), .clk(CLK));  // open: clr
  or or_2 (or_2_out, decoder_1_out1, RST);
  or or_3 (or_3_out, POP, RST, WE);
  Multiplexer #(.width(16), .disabled(0), .enable("false")) multiplexer_3 (
    .in0({H_q, L_q}), .in1(ram_1_data), .out(multiplexer_3_out), .sel(POP));
  and and_1 (and_1_out, ~RST, OE);  // AND_Gate
  RAM #(.dataWidth(16), .bus("separate")) ram_1 (
    .addr(counter_1_q), .din(counter_2_q), .data(ram_1_data), .str(PUSH), .clk(CLK), .clr(RST));  // open: sel, ld
  Counter #(.width(16), .max('hffff), .trigger("falling")) counter_2 (
    .load(or_3_out), .D(multiplexer_3_out), .count(and_1_out), .Q(counter_2_q), .clk(CLK));  // open: carry, clr
  assign A = buffer_1_out ? counter_2_q : 16'bz;  // Controlled_Buffer controlled_buffer_1
  buf buffer_1 (buffer_1_out, buffer_2_out);
  buf buffer_2 (buffer_2_out, OE);

  // Notes on the sheet:
  //   OE: pull=down
  //   POP: pull=down
  //   RST: pull=down
  //   WE: pull=down
  //   L_H: pull=down
  //   PUSH: pull=down
  //   CLK: pull=down
endmodule

module Control_Unit (
  input  CLK,
  input  RST,
  input  [7:0] II,
  input  INTR,
  input  [4:0] CND,
  output [15:0] AO,
  output DT_nR,
  output DEN,
  output MEMW,
  output MEMR,
  output IOW,
  output IOR,
  output INTA,
  output ALU_REG_EN,
  output REGs_WE,
  output ALU_REG_I_O,
  output [2:0] REGs_DDD,
  output ALU_REG_a_b,
  output REGs_RE,
  output ALU_Flag_Read,
  output [2:0] REGs_SSS,
  output ALU_OE,
  output REGs_Acc_select,
  output REGs_AO,
  output [3:0] ALU_CODE,
  output AS_PC_WE,
  output AS_PC_OE,
  output AS_PC_L_H,
  output AS_PC_PUSH,
  output FR_OE,
  output AS_PC_POP,
  output FR_WE,
  output [1:0] FS,
  output Stack_PUSH,
  output Stack_POP
);

  wire and_1_out, and_2_out, d_ff_1_q, decoder_2_out0, decoder_2_out1, decoder_2_out2, decoder_2_out3,
       decoder_3_out0, decoder_3_out3, decoder_3_out4, END, HLT, \int , multiplexer_7_out, nor_1_out,
       not_1_out, or_1_out, or_2_out, or_3_out, xor_2_out;
  wire [1:0] multiplexer_6_out_2, multiplexer_6_out_3;
  wire [2:0] multiplexer_9_out, SSS, status;
  wire [3:0] decoder_1_out0, multiplexer_2_out, multiplexer_4_out, not_2_out, xor_1_out;
  wire [3:3] pull_resistor_2_node;
  wire [7:0] controlled_buffer_1_out, counter_1_q, INSTRUCTION, multiplexer_1_out;
  wire [7:6] IR_q;
  wire [15:0] interrupt_vector_decoder_1_address;
  wire [15:8] pull_resistor_3_node;
  wire [26:0] multiplexer_6_out;
  wire [31:0] rom_1_data;

  and and_1 (and_1_out, CLK, ~HLT);  // AND_Gate
  assign controlled_buffer_1_out = nor_1_out ? INSTRUCTION : 8'bz;  // Controlled_Buffer controlled_buffer_1
  Pull_Resistor pull_resistor_1 (.node(controlled_buffer_1_out));
  Multiplexer #(.width(8), .enable("false")) multiplexer_1 (
    .in0(II), .in1(8'h2a), .out(multiplexer_1_out), .sel(\int ));
  D_Flip_Flop #(.trigger("falling")) d_ff_1 (.clk(CLK), .D(\int ), .Q(d_ff_1_q), .reset(CLK));  // open: Qn, preset, en
  Multiplexer #(.select(2), .width(4), .enable("false")) multiplexer_2 (
    .in0(4'b0000), .in1(4'b1100), .in2(4'b1110), .in3({2'b11, FS[0], REGs_DDD[0]}), .out(multiplexer_2_out),
    .sel(multiplexer_6_out_3));
  Multiplexer #(.width(4), .disabled(0), .enable("false")) multiplexer_3 (
    .in0(multiplexer_2_out), .in1({pull_resistor_2_node[3], FS, REGs_DDD[0]}), .out(ALU_CODE),
    .sel(multiplexer_6_out[26]));
  Pull_Resistor pull_resistor_2 (.node({pull_resistor_2_node[3], FS, REGs_DDD[0]}));
  nor nor_1 (nor_1_out, counter_1_q[0], counter_1_q[1], counter_1_q[2], counter_1_q[3], counter_1_q[4], counter_1_q[5], counter_1_q[6], counter_1_q[7]);
  not not_1 (not_1_out, END);
  assign not_2_out = ~CND[3:0];  // NOT_Gate not_2, 4 bits wide
  Register IR (.D(multiplexer_1_out), .en(decoder_2_out1), .Q({IR_q, FS, REGs_DDD[0], SSS}), .clk(CLK), .clr(RST));
  Counter #(.trigger("falling")) counter_1 (
    .load(END), .D(controlled_buffer_1_out), .count(not_1_out), .Q(counter_1_q), .clk(and_1_out), .clr(RST));  // open: carry
  Multiplexer #(.width(4), .enable("false")) multiplexer_4 (
    .in0(not_2_out), .in1(CND[3:0]), .out(multiplexer_4_out), .sel(FS[1]));
  Decoder #(.select(2), .enable("false")) decoder_1 (
    .out0(decoder_1_out0[0]), .out1(decoder_1_out0[1]), .out2(decoder_1_out0[2]), .out3(decoder_1_out0[3]),
    .sel({FS[0], REGs_DDD[0]}));
  Pull_Resistor pull_resistor_3 (.node({pull_resistor_3_node, IR_q, FS, REGs_DDD[0], SSS}));
  Multiplexer #(.width(16)) multiplexer_5 (
    .in0({pull_resistor_3_node, IR_q, FS, REGs_DDD[0], SSS}), .in1(interrupt_vector_decoder_1_address),
    .out(AO), .sel(decoder_2_out3), .en(or_1_out));
  Interrupt_Vector_Decoder interrupt_vector_decoder_1 (
    .vector(multiplexer_1_out), .address(interrupt_vector_decoder_1_address), .CLK(CLK), .RST(RST),
    .\reg (decoder_2_out0), .inc(decoder_2_out3));
  or or_1 (or_1_out, decoder_2_out3, decoder_2_out2);
  Decoder #(.select(2), .disabled(0), .enable("false")) decoder_2 (
    .out0(decoder_2_out0), .out1(decoder_2_out1), .out2(decoder_2_out2), .out3(decoder_2_out3),
    .sel(multiplexer_6_out_2));
  assign xor_1_out = multiplexer_4_out ^ decoder_1_out0;  // XOR_Gate xor_1, 4 bits wide
  Multiplexer #(.width(32), .enable("false")) multiplexer_6 (
    .in0(rom_1_data), .in1(32'h200001),
    .out({ALU_REG_EN, ALU_REG_I_O, ALU_REG_a_b, ALU_Flag_Read, ALU_OE, multiplexer_6_out[26], multiplexer_6_out_3, FR_OE, FR_WE, multiplexer_6_out_2[0], multiplexer_6_out_2[1], REGs_WE, REGs_RE, REGs_Acc_select, REGs_AO, AS_PC_WE, AS_PC_OE, AS_PC_L_H, AS_PC_PUSH, AS_PC_POP, status, Stack_PUSH, Stack_POP, multiplexer_6_out[5:3], HLT, multiplexer_6_out[1:0]}),
    .sel(\int ));
  ROM #(.dataWidth(32)) rom_1 (.addr(counter_1_q), .data(rom_1_data));  // open: sel
  Multiplexer #(.select(2), .enable("false")) multiplexer_7 (
    .in0(xor_1_out[0]), .in1(xor_1_out[1]), .in2(xor_1_out[2]), .in3(xor_1_out[3]), .out(multiplexer_7_out),
    .sel({FS[0], REGs_DDD[0]}));
  xor xor_2 (xor_2_out, multiplexer_6_out_3[0], multiplexer_6_out_3[1]);
  D_Flip_Flop #(.trigger("falling")) d_ff_2 (.clk(CLK), .D(and_2_out), .Q(\int ), .reset(RST));  // open: Qn, preset, en
  ROM rom_2 (.addr({IR_q, FS, REGs_DDD[0], SSS}), .data(INSTRUCTION), .sel(decoder_2_out1));
  Multiplexer #(.enable("false")) multiplexer_8 (
    .in0(multiplexer_6_out[0]), .in1(multiplexer_7_out), .out(END), .sel(multiplexer_6_out[1]));
  // Probe on SSS
  // Probe on {FS, REGs_DDD[0]}
  Multiplexer #(.width(3), .enable("false")) multiplexer_9 (
    .in0(status), .in1(3'b111), .out(multiplexer_9_out), .sel(d_ff_1_q));
  Multiplexer #(.width(3), .enable("false")) multiplexer_10 (
    .in0(SSS), .in1({FS, REGs_DDD[0]}), .out(REGs_SSS), .sel(or_2_out));
  or or_2 (or_2_out, xor_2_out, Stack_PUSH);
  and and_2 (and_2_out, ~nor_1_out, INTR, CND[4], or_3_out);  // AND_Gate
  or or_3 (or_3_out, END, HLT);
  Decoder #(.select(3), .enable("false")) decoder_3 (
    .out0(decoder_3_out0), .out1(MEMW), .out2(MEMR), .out3(decoder_3_out3), .out4(decoder_3_out4),
    .out5(IOW), .out6(IOR), .out7(INTA), .sel(multiplexer_9_out));
  or or_4 (DT_nR, decoder_3_out0, MEMW, decoder_3_out3, decoder_3_out4, IOW);
  or or_5 (DEN, MEMW, MEMR, IOW, IOR, INTA);

  assign REGs_DDD[2:1] = FS;

  // Other names for the same wires on the sheet: COD[2:0] = {FS, REGs_DDD[0]}; COND[2:0] = {FS, REGs_DDD[0]};
  //   DDD[2:0] = {FS, REGs_DDD[0]}

  // Notes on the sheet:
  //   RST: pull=down
  //   ALU_REG_a_b: pull=down
  //   REGs_SSS: pull=down
  //   ALU_REG_EN: pull=down
  //   AS_PC_L_H: pull=down
  //   ALU_CODE: pull=down
  //   REGs_DDD: pull=down
  //   INTR: pull=down
  //   REGs_AO: pull=down
  //   ALU_REG_I_O: pull=down
  //   REGs_WE: pull=down
  //   FR_OE: pull=down
  //   CLK: pull=down
  //   ALU_Flag_Read: pull=down
  //   DEN: pull=down
  //   AS_PC_OE: pull=down
  //   REGs_RE: pull=down
  //   DT_nR: pull=down
  //   AS_PC_WE: pull=down
  //   AS_PC_PUSH: pull=down
  //   CND: pull=down
  //   AS_PC_POP: pull=down
  //   MICROCODE
  //   contents of rom_1 (hex, n*v repeats v):
  //   204201 c0001 90201 50101 84201 a0004200 e0010101 81040000 19080001 82040000 1a080001 a0040000
  //   84060000 1c0a0001 a0010200 84060000 1c0a0001 a0004200 84060000 1c0a0001 83060000 1b0a0001 a0004200
  //   e200 e0008001 a0004200 80004202 e0008000 c000a001 a0004200 80004200 e0009000 c000a001 a0004200
  //   80004202 e0009000 c000a001 801 2 801 40081 10281 4281 80041 10141 1a0601 160501 4200 901080 f08200
  //   30a201 400841 c00001 202*0 304
  //   DECODER
  //   contents of rom_2 (hex, n*v repeats v):
  //   7 9 14 26 11 34 4 ff 7 9 14 26 11 ff 4 ff 7 9 14 26 11 34 4 ff 7 9 14 26 11 ff 4 ff 7 9 25 26 11 34
  //   4 ff 7 9 2f 26 11 ff 4 ff 7 9 2a 26 11 34 4 ff 16 1d 33 26 11 ff 5 ff 19 2d 21 2d 28 2d 2b 2d 19 2d
  //   21 2d 28 2d 2b 2d 19 2d 21 2d 28 2d 2b 2d 19 2d 21 2d 28 2d 2b 2d 19 2e 21 2e 28 2e 2b 2e 19 2e 21
  //   2e 28 2e 2b 2e 19 2e 21 2e 28 2e 2b 2e 19 2e 21 2e 29 2e 2c 2e 7*b e 7*b e 7*b e 7*b e 7*b e 7*b e
  //   7*b e 7*b e 7*1 2 7*1 2 7*1 2 7*1 2 7*1 2 7*1 2 7*1 2 7*3 ff
endmodule

module Interrupt_Vector_Decoder (
  input  CLK,
  input  RST,
  input  [7:0] vector,
  input  \reg ,
  input  inc,
  output [15:0] address
);

  wire buffer_1_out, or_1_out;
  wire [7:0] register_1_q;
  wire [15:0] shifter_1_out, t_ff_1_q;
  wire [15:8] pull_resistor_1_node;

  Register register_1 (.D(vector), .en(\reg ), .Q(register_1_q), .clk(CLK), .clr(RST));
  Pull_Resistor pull_resistor_1 (.node({pull_resistor_1_node, register_1_q}));
  T_Flip_Flop #(.trigger("falling")) t_ff_1 (
    .clk(CLK), .T(inc), .Q(t_ff_1_q[0]), .reset(or_1_out), .en(buffer_1_out));  // open: Qn, preset
  buf buffer_1 (buffer_1_out, inc);
  or or_1 (or_1_out, RST, ~inc);  // OR_Gate
  Pull_Resistor pull_resistor_2 (.node(t_ff_1_q));
  Shifter #(.width(16)) shifter_1 (.in({pull_resistor_1_node, register_1_q}), .\dist (4'b0001), .out(shifter_1_out));
  assign address = t_ff_1_q | shifter_1_out;  // OR_Gate or_2, 16 bits wide

  // Notes on the sheet:
  //   reg: pull=down
  //   inc: pull=down
  //   RST: pull=down
  //   vector: pull=down
  //   CLK: pull=down
endmodule

module Data_Stack (
  input  CLK,
  input  RST,
  input  [7:0] IN,
  input  PUSH,
  input  POP,
  output [7:0] OUT
);

  wire multiplexer_1_out, not_1_out, not_2_out, or_1_out;
  wire [7:0] counter_1_q, register_1_q;

  or or_1 (or_1_out, PUSH, POP);
  not not_1 (not_1_out, CLK);
  Multiplexer #(.disabled(0), .enable("false")) multiplexer_1 (
    .in0(not_1_out), .in1(CLK), .out(multiplexer_1_out), .sel(POP));
  Counter counter_1 (
    .load(POP), .count(or_1_out), .Q(counter_1_q), .clk(multiplexer_1_out), .clr(RST));  // open: D, carry
  Register #(.trigger("high")) register_1 (.D(IN), .Q(register_1_q), .clk(CLK), .clr(RST));  // open: en
  RAM #(.bus("separate")) ram_1 (
    .addr(counter_1_q), .din(register_1_q), .data(OUT), .str(PUSH), .clk(not_2_out), .ld(POP), .clr(RST));  // open: sel
  not not_2 (not_2_out, CLK);

  // Notes on the sheet:
  //   PUSH: pull=down
  //   IN: pull=down
  //   RST: pull=down
  //   POP: pull=down
  //   CLK: pull=down
endmodule

module Bus_Controller (
  input  M_IO,
  input  S1,
  input  S0,
  output MEMW,
  output MEMR,
  output IOW,
  output IOR,
  output INTA,
  output DT_nR
);

  wire decoder_1_out0, decoder_1_out3, decoder_1_out4;

  Decoder #(.select(3), .enable("false")) decoder_1 (
    .out0(decoder_1_out0), .out1(MEMW), .out2(MEMR), .out3(decoder_1_out3), .out4(decoder_1_out4),
    .out5(IOW), .out6(IOR), .out7(INTA), .sel({M_IO, S1, S0}));
  or or_1 (DT_nR, decoder_1_out0, MEMW, decoder_1_out3, decoder_1_out4, IOW);

  // Notes on the sheet:
  //   M_IO: pull=down
  //   S0: pull=down
  //   S1: pull=down
endmodule

module RAM_64k (
  input  [15:0] A,
  input  [7:0] Di,
  input  CLK,
  input  CLR,
  input  MEMW,
  input  MEMR,
  output [7:0] Do
);

  wire [7:0] ram_1_data;

  RAM #(.addrWidth(16), .bus("separate")) ram_1 (
    .addr(A), .din(Di), .data(ram_1_data), .str(MEMW), .clk(CLK), .clr(CLR));  // open: sel, ld
  assign Do = MEMR ? ram_1_data : 8'bz;  // Controlled_Buffer controlled_buffer_1

  // Notes on the sheet:
  //   MEMR: pull=down
  //   MEMW: pull=down
  //   Di: pull=down
  //   CLK: pull=down
  //   CLR: pull=down
endmodule

module RAM_16k (
  input  [13:0] A,
  input  [7:0] Di,
  input  CLK,
  input  CLR,
  input  MEMW,
  input  MEMR,
  output [7:0] Do
);

  RAM #(.addrWidth(14), .bus("separate")) ram_1 (
    .addr(A), .din(Di), .data(Do), .str(MEMW), .clk(CLK), .ld(MEMR), .clr(CLR));  // open: sel

  // Notes on the sheet:
  //   MEMR: pull=down
  //   CLK: pull=down
  //   MEMW: pull=down
  //   Di: pull=down
  //   A: pull=down
  //   CLR: pull=down
endmodule

module RAM_8k (
  input  [12:0] A,
  input  [7:0] Di,
  input  CLK,
  input  CLR,
  input  MEMW,
  input  MEMR,
  output [7:0] Do
);

  RAM #(.addrWidth(13), .bus("separate")) ram_1 (
    .addr(A), .din(Di), .data(Do), .str(MEMW), .clk(CLK), .ld(MEMR), .clr(CLR));  // open: sel

  // Notes on the sheet:
  //   MEMR: pull=down
  //   CLK: pull=down
  //   MEMW: pull=down
  //   CLR: pull=down
  //   A: pull=down
  //   Di: pull=down
endmodule

module ROM_8k (
  input  [12:0] A,
  input  CS,
  output [7:0] D
);

  wire [7:0] rom_1_data;

  ROM #(.addrWidth(13)) rom_1 (.addr(A), .data(rom_1_data));  // open: sel
  assign D = CS ? rom_1_data : 8'bz;  // Controlled_Buffer controlled_buffer_1

  // Notes on the sheet:
  //   CS: pull=down
  //   contents of rom_1 (hex, n*v repeats v):
  //   38 40 e2 ff 44 4c 76 6e c7 30 48 e e0 28 6c 74 eb f4 f8 20 48 18 e0 18 11 48 6 e0 76 6e 22 3f e0 3f
  //   e0 3f e0 7c e0 d0 e0 4f e1 40 e0 ee e1 3f e0 3f e0 3f e0 3f e0 3f e0 3f e0 3f e0 3f e0 3a 2e 2 36 0
  //   c7 3a 42 4f 4f 54 20 46 41 49 4c 55 52 45 2c 20 49 4e 53 45 52 54 20 53 59 53 54 45 4d 20 53 54 4f
  //   52 41 47 45 20 41 4e 44 20 50 52 45 53 53 20 41 4e 59 20 4b 45 59 a 35 6 0 2a 7 e 0 6 1 2a 7 44 24
  //   80 46 68 93 e0 24 40 48 9d e0 8 6 5 91 48 83 e0 38 b5 e0 4c 6 2 16 1 1e 0 26 0 2e c 36 0 2a 7 4e 3c
  //   ab 68 0 c 38 93 e0 6 3 e 0 16 36 2e e0 36 46 2a 4 6 0 2a 5 6 1 e a 16 1 2a 4 38 7c e0 5c 64 6c 74 b0
  //   68 e9 e0 1 68 ef e0 1 68 f8 e0 1 68 26 e1 76 6e 66 5e 3a 6 c 69 38 e4 e0 c1 69 11 48 f0 e0 38 e4 e0
  //   54 c1 16 0 1e 0 38 3 e1 16 0 14 a 60 c e1 10 38 3 e1 4 a 34 30 44 18 c2 3c a 40 1 e1 34 30 44 18 46
  //   69 19 48 1c e1 56 38 e4 e0 c1 b0 68 32 e1 1 68 40 e1 38 e4 e0 c7 69 30 48 39 e1 28 11 48 32 e1 38 e4
  //   e0 c7 3c 24 68 e4 e0 69 30 48 4c e1 28 38 40 e1 3c c 68 e9 e1 b0 68 69 e1 1 68 6f e1 1 68 76 e1 1 68
  //   7e e1 1 68 a2 e1 3a 4b b0 68 69 e1 3a 4b b0 68 6f e1 69 3a 46 6 11 6b 4b b0 35 22 4c 54 16 0 cf 30
  //   48 88 e1 28 6c 74 30 48 8f e1 28 4b b0 68 8f e1 f8 3c a 68 e1 e1 10 9 68 e1 e1 38 8a e1 4c 54 16 0
  //   cf 30 48 ac e1 28 6c 74 30 48 b3 e1 28 4b b0 68 b3 e1 3c a 68 e1 e1 3c 8 68 cc e1 10 9 68 e1 e1 f8
  //   69 38 ae e1 44 c2 b0 68 b3 e1 11 8 46 69 c6 14 1 f0 40 b3 e1 29 38 b3 e1 f8 69 76 6e fa 56 4e 3a 6b
  //   c1 38 4f e1 b0 68 7 e2 44 6 3 91 46 60 6 e2 1 68 b e2 1 68 f e2 1 68 24 e2 3a 6 4 6f 3a c1 6f 4f 3a
  //   39 39 e2 e 0 4d f8 30 48 1b e2 28 9 48 14 e2 11 48 12 e2 3a 39 39 e2 e 0 c7 6d 30 48 30 e2 28 9 48
  //   29 e2 11 48 27 e2 3a c1 6f c3 6d c4 6d 22 25 6 ff c8 d1 da e3 ec f5 ae 48 3 e0 36 0 2e 0 16 ff 6 55
  //   f8 bf 48 66 e2 10 c6 4 ff f0 c5 c 3 e8 38 53 e2 2e 2 36 0 fa 16 10 1e 0 26 0 6 e0 e 1f 39 4 e0 35 38
  //   f2 e2 4c 53 43 2d 38 20 42 49 4f 53 20 28 43 29 2c 20 56 45 52 20 31 2e 30 2c 20 32 30 32 30 a a 20
  //   4b 42 20 52 41 4d a a 53 54 4f 52 41 47 45 20 23 20 3a 20 4e 4f 4e 45 45 52 52 4f 52 20 52 4f 20 56
  //   4f 4c 20 46 49 58 45 44 20 52 45 4d 4f 56 41 42 4c 45 20 44 52 49 56 45 31 32 38 4b 35 31 32 4b 20
  //   20 31 4d 20 20 32 4d 20 20 34 4d 20 20 38 4d 20 31 36 4d 6 0 2a 4 6 3 e 0 16 1f 2e e2 36 7c 2a 4 2a
  //   6 c8 6 2 2a 4 6 3 e 0 16 8 2e e2 36 9b 2a 4 6 0 2a 7 e 0 e1 6 3 e 0 16 a 2e e2 36 a3 2a 4 6 30 84 c8
  //   6 1 16 1 2a 4 6 3 e 0 16 3 2e e2 36 ad 2a 4 cc 6 1 2a 7 44 24 80 46 68 d9 e3 44 24 7 1 68 f9 e3 1 68
  //   8 e4 1 68 17 e4 1 68 26 e4 1 68 35 e4 1 68 44 e4 1 68 53 e4 38 e9 e3 46 44 24 10 68 bb e3 6 3 e 0 16
  //   a 2e e2 36 c6 2a 4 46 44 24 40 68 ab e3 46 24 8 68 ca e3 6 3 e 0 16 4 2e e2 36 bc 2a 4 cc 8 6 4 91
  //   48 1b e3 6 1 e a 16 2 2a 4 38 7c e0 6 3 e 0 16 6 2e e2 36 d0 2a 4 46 38 98 e3 6 3 e 0 16 6 2e e2 36
  //   c0 2a 4 38 86 e3 6 3 e 0 16 3 2e e2 36 b9 2a 4 38 98 e3 6 3 e 0 16 4 2e e2 36 b0 2a 4 46 38 98 e3 6
  //   3 e 0 16 5 2e e2 36 b4 2a 4 46 38 98 e3 6 3 e 0 16 4 2e e2 36 d6 2a 4 38 6c e3 6 3 e 0 16 4 2e e2 36
  //   da 2a 4 38 6c e3 6 3 e 0 16 4 2e e2 36 de 2a 4 38 6c e3 6 3 e 0 16 4 2e e2 36 e2 2a 4 38 6c e3 6 3 e
  //   0 16 4 2e e2 36 e6 2a 4 38 6c e3 6 3 e 0 16 4 2e e2 36 ea 2a 4 38 6c e3 6 3 e 0 16 4 2e e2 36 ee 2a
  //   4 38 6c e3
endmodule

module RAM_ROM_Select (
  input  [15:0] A,
  input  MEMW,
  input  MEMR,
  output [15:0] RAMA,
  output [12:0] ROMA,
  output MEMW_2,
  output MEMR_2,
  output ROMR
);

  wire and_1_out;
  wire [1:1] demultiplexer_1_out1;
  wire [15:0] buffer_1_out;

  assign buffer_1_out = A;  // Buffer buffer_1, 16 bits wide
  Pull_Resistor pull_resistor_1 (.node(buffer_1_out));
  and and_1 (and_1_out, buffer_1_out[13], buffer_1_out[14], buffer_1_out[15]);
  Demultiplexer #(.width(2), .enable("false")) demultiplexer_1 (
    .out0({MEMW_2, MEMR_2}), .out1({demultiplexer_1_out1[1], ROMR}), .in({MEMW, MEMR}), .sel(and_1_out));

  assign RAMA = A;
  assign ROMA = A[12:0];

  // Notes on the sheet:
  //   MEMR: pull=down
  //   MEMW: pull=down
endmodule

module delayer_25 (
  input  in,
  output out
);

  wire buffer_1_out, buffer_2_out, buffer_3_out, buffer_4_out, buffer_5_out, buffer_6_out, buffer_7_out,
       buffer_8_out, buffer_9_out, buffer_10_out, buffer_11_out, buffer_12_out, buffer_13_out, buffer_14_out,
       buffer_15_out, buffer_16_out, buffer_17_out, buffer_18_out, buffer_19_out, buffer_20_out,
       buffer_21_out, buffer_22_out, buffer_23_out, buffer_25_out;

  buf buffer_1 (buffer_1_out, buffer_2_out);
  buf buffer_2 (buffer_2_out, in);
  buf buffer_3 (buffer_3_out, buffer_1_out);
  buf buffer_4 (buffer_4_out, buffer_7_out);
  buf buffer_5 (buffer_5_out, buffer_6_out);
  buf buffer_6 (buffer_6_out, buffer_3_out);
  buf buffer_7 (buffer_7_out, buffer_5_out);
  buf buffer_8 (buffer_8_out, buffer_10_out);
  buf buffer_9 (buffer_9_out, buffer_4_out);
  buf buffer_10 (buffer_10_out, buffer_9_out);
  buf buffer_11 (buffer_11_out, buffer_8_out);
  buf buffer_12 (buffer_12_out, buffer_13_out);
  buf buffer_13 (buffer_13_out, buffer_15_out);
  buf buffer_14 (buffer_14_out, buffer_12_out);
  buf buffer_15 (buffer_15_out, buffer_11_out);
  buf buffer_16 (buffer_16_out, buffer_19_out);
  buf buffer_17 (buffer_17_out, buffer_16_out);
  buf buffer_18 (buffer_18_out, buffer_14_out);
  buf buffer_19 (buffer_19_out, buffer_18_out);
  buf buffer_20 (buffer_20_out, buffer_17_out);
  buf buffer_21 (buffer_21_out, buffer_23_out);
  buf buffer_22 (buffer_22_out, buffer_20_out);
  buf buffer_23 (buffer_23_out, buffer_22_out);
  buf buffer_24 (out, buffer_25_out);
  buf buffer_25 (buffer_25_out, buffer_21_out);

  // Notes on the sheet:
  //   in: pull=down
endmodule

module Interrupt_Controller (
  input  IR7,
  input  IR6,
  input  IR5,
  input  IR4,
  input  IR3,
  input  IR2,
  input  IR1,
  input  IR0,
  input  RESET,
  input  INTA,
  output [7:0] D,
  output INT
);

  wire and_1_out, decoder_1_out0, decoder_1_out1, decoder_1_out2, decoder_1_out3, decoder_1_out4,
       decoder_1_out5, decoder_1_out6, decoder_1_out7, IR0_q, IR1_q, IR2_q, IR3_q, IR4_q, IR5_q, IR6_q,
       IR7_q, not_2_out, or_1_out, or_2_out, or_3_out, or_4_out, or_5_out, or_6_out, or_7_out, or_8_out;
  wire [2:0] not_1_out, priority_encoder_1_out, register_1_q;

  D_Flip_Flop u_IR7 (.clk(IR7), .D(1'b1), .Q(IR7_q), .reset(or_1_out));  // open: Qn, preset, en
  or or_1 (or_1_out, RESET, decoder_1_out7);
  D_Flip_Flop u_IR6 (.clk(IR6), .D(1'b1), .Q(IR6_q), .reset(or_2_out));  // open: Qn, preset, en
  or or_2 (or_2_out, RESET, decoder_1_out6);
  D_Flip_Flop u_IR5 (.clk(IR5), .D(1'b1), .Q(IR5_q), .reset(or_3_out));  // open: Qn, preset, en
  or or_3 (or_3_out, RESET, decoder_1_out5);
  D_Flip_Flop u_IR4 (.clk(IR4), .D(1'b1), .Q(IR4_q), .reset(or_4_out));  // open: Qn, preset, en
  or or_4 (or_4_out, RESET, decoder_1_out4);
  D_Flip_Flop u_IR3 (.clk(IR3), .D(1'b1), .Q(IR3_q), .reset(or_5_out));  // open: Qn, preset, en
  or or_5 (or_5_out, RESET, decoder_1_out3);
  D_Flip_Flop u_IR2 (.clk(IR2), .D(1'b1), .Q(IR2_q), .reset(or_6_out));  // open: Qn, preset, en
  or or_6 (or_6_out, RESET, decoder_1_out2);
  D_Flip_Flop u_IR1 (.clk(IR1), .D(1'b1), .Q(IR1_q), .reset(or_7_out));  // open: Qn, preset, en
  or or_7 (or_7_out, RESET, decoder_1_out1);
  D_Flip_Flop u_IR0 (.clk(IR0), .D(1'b1), .Q(IR0_q), .reset(or_8_out));  // open: Qn, preset, en
  or or_8 (or_8_out, RESET, decoder_1_out0);
  Decoder #(.select(3), .disabled(0)) decoder_1 (
    .out0(decoder_1_out0), .out1(decoder_1_out1), .out2(decoder_1_out2), .out3(decoder_1_out3),
    .out4(decoder_1_out4), .out5(decoder_1_out5), .out6(decoder_1_out6), .out7(decoder_1_out7),
    .sel(register_1_q), .en(and_1_out));
  and and_1 (and_1_out, INTA, INT);
  Priority_Encoder #(.disabled(0)) priority_encoder_1 (
    .in0(IR7_q), .in1(IR6_q), .in2(IR5_q), .in3(IR4_q), .in4(IR3_q), .in5(IR2_q), .in6(IR1_q), .in7(IR0_q),
    .out(priority_encoder_1_out), .gs(INT));  // open: en_in, en_out
  assign not_1_out = ~priority_encoder_1_out;  // NOT_Gate not_1, 3 bits wide
  Register #(.width(3), .trigger("high")) register_1 (
    .D(not_1_out), .en(INT), .Q(register_1_q), .clk(not_2_out), .clr(RESET));
  not not_2 (not_2_out, and_1_out);
  ROM #(.addrWidth(3)) rom_1 (.addr(register_1_q), .data(D), .sel(INTA));

  // Notes on the sheet:
  //   INT CODE
endmodule

module VideoCard (
  input  [7:0] Di,
  input  [15:0] A,
  input  CLK,
  input  RST,
  input  IOW,
  input  IOR,
  output [6:0] ASCII,
  output STROBE,
  output reset,
  output [7:0] Do
);

  wire and_1_out, and_2_out, and_3_out;
  wire [7:0] pull_resistor_1_node;
  wire [7:7] register_1_q;

  and and_1 (and_1_out, ~A[1], ~A[2], A[3], ~A[4]);  // AND_Gate
  and and_2 (and_2_out, IOR, and_1_out);
  Pull_Resistor pull_resistor_1 (.node(pull_resistor_1_node));
  assign Do = and_2_out ? pull_resistor_1_node : 8'bz;  // Controlled_Buffer controlled_buffer_1
  Register #(.trigger("falling")) register_1 (
    .D(Di), .en(and_3_out), .Q({register_1_q[7], ASCII}), .clk(CLK), .clr(RST));
  and and_3 (and_3_out, and_1_out, IOW);
  not not_1 (STROBE, and_3_out);

  assign reset = RST;

  // Notes on the sheet:
  //   RST: pull=down
  //   IOR: pull=down
  //   CLK: pull=down
  //   IOW: pull=down
  //   Di: pull=down
  //   A: pull=down
  //   PORT 4
endmodule

module Keyboard_Controller (
  input  IOR,
  input  [15:0] A,
  input  [6:0] ASCII,
  input  IOW,
  input  [7:0] Di,
  input  RST,
  output STROBE,
  output [7:0] Do,
  output reset
);

  wire and_1_out, and_2_out, and_3_out, and_4_out, and_5_out, d_ff_1_qn, or_1_out;
  wire [7:0] pull_resistor_1_node, register_1_q;
  wire [7:7] pull_resistor_2_node;

  and and_1 (and_1_out, A[1], ~A[2], A[3], ~A[4]);  // AND_Gate
  and and_2 (and_2_out, IOR, and_1_out);
  and and_3 (and_3_out, IOW, and_1_out);
  Pull_Resistor pull_resistor_1 (.node(pull_resistor_1_node));
  assign pull_resistor_1_node = and_3_out ? Di : 8'bz;  // Controlled_Buffer controlled_buffer_1
  Pull_Resistor pull_resistor_2 (.node({pull_resistor_2_node[7], ASCII}));
  or or_1 (or_1_out, and_3_out, and_2_out);
  and and_4 (and_4_out, pull_resistor_1_node[0], ~pull_resistor_1_node[1], ~pull_resistor_1_node[2], ~pull_resistor_1_node[3], pull_resistor_1_node[4], ~pull_resistor_1_node[5], ~pull_resistor_1_node[6], ~pull_resistor_1_node[7]);  // AND_Gate
  and and_5 (and_5_out, ~pull_resistor_1_node[0], ~pull_resistor_1_node[1], pull_resistor_1_node[2], pull_resistor_1_node[3], ~pull_resistor_1_node[4], ~pull_resistor_1_node[5], ~pull_resistor_1_node[6], ~pull_resistor_1_node[7]);  // AND_Gate
  Register register_1 (
    .D({pull_resistor_2_node[7], ASCII}), .en(and_2_out), .Q(register_1_q), .clk(and_2_out), .clr(reset));
  D_Flip_Flop #(.trigger("falling")) d_ff_1 (
    .clk(or_1_out), .D(and_4_out), .Qn(d_ff_1_qn));  // open: Q, preset, en, reset
  or or_2 (reset, and_5_out, RST);
  Pull_Resistor pull_resistor_3 (.node(STROBE));
  assign STROBE = d_ff_1_qn ? and_2_out : 1'bz;  // Controlled_Buffer controlled_buffer_2
  assign Do = and_2_out ? register_1_q : 8'bz;  // Controlled_Buffer controlled_buffer_3

  // Notes on the sheet:
  //   A: pull=down
  //   RST: pull=down
  //   ASCII: pull=down
  //   IOW: pull=down
  //   Di: pull=down
  //   IOR: pull=down
  //   PORT 5
  //   11h code for read buffer with save him
  //   0Ch code for clear buffer
endmodule

module Storage_Controller (
  input  [7:0] Di,
  input  IOW,
  input  [15:0] A,
  input  IOR,
  input  CLK,
  input  RST,
  input  [7:0] param,
  input  [7:0] Dr,
  output [7:0] Dw,
  output [23:0] Ao,
  output A_2,
  output B,
  output C,
  output D,
  output WRITE,
  output indicate,
  output READ,
  output [7:0] Do
);

  wire and_1_out, and_2_out, and_3_out, and_4_out, and_5_out, and_6_out, BYTES_carry, counter_1_carry,
       d_i_o_out, decoder_1_out0, decoder_1_out1, decoder_1_out2, LOW_carry, or_1_out, or_2_out, or_3_out;
  wire [1:0] counter_1_q;
  wire [7:0] DOR_q;

  and d_i_o (d_i_o_out, ~A[1], A[2], A[3], ~A[4]);  // AND_Gate
  and and_1 (and_1_out, A[1], A[2], A[3], ~A[4]);  // AND_Gate
  and and_2 (and_2_out, IOW, d_i_o_out);
  and and_3 (and_3_out, IOW, and_1_out);
  and and_4 (and_4_out, d_i_o_out, IOR);
  and and_5 (and_5_out, and_1_out, IOR);
  Register #(.trigger("falling")) DOR (.D(Di), .en(and_3_out), .Q(DOR_q), .clk(CLK), .clr(or_1_out));
  or or_1 (or_1_out, RST, DOR_q[2]);
  Counter #(.width(2), .max('h2), .ongoal("stay"), .trigger("falling")) counter_1 (
    .Q(counter_1_q), .carry(counter_1_carry), .clk(and_2_out), .clr(or_1_out));  // open: load, D, count
  and and_6 (and_6_out, CLK, and_2_out);
  assign Do = and_5_out ? param : 8'bz;  // Controlled_Buffer controlled_buffer_1
  assign Do = and_4_out ? Dr : 8'bz;  // Controlled_Buffer controlled_buffer_2
  or or_2 (or_2_out, and_6_out, and_4_out);
  Decoder #(.select(2), .disabled(0)) decoder_1 (
    .out0(decoder_1_out0), .out1(decoder_1_out1), .out2(decoder_1_out2), .sel(counter_1_q), .en(and_2_out));  // open: out3
  Counter #(.trigger("falling")) BYTES (
    .count(counter_1_carry), .Q(Ao[7:0]), .carry(BYTES_carry), .clk(or_2_out), .clr(or_3_out));  // open: load, D
  or or_3 (or_3_out, decoder_1_out0, decoder_1_out1, or_1_out);
  and and_7 (WRITE, counter_1_carry, and_2_out);
  and and_8 (READ, counter_1_carry, and_4_out);
  assign Dw = decoder_1_out2 ? Di : 8'bz;  // Controlled_Buffer controlled_buffer_3
  Counter #(.trigger("falling")) LOW (
    .load(decoder_1_out1), .D(Di), .count(BYTES_carry), .Q(Ao[15:8]), .carry(LOW_carry), .clk(or_2_out),
    .clr(or_1_out));
  Counter #(.trigger("falling")) HIGH (
    .load(decoder_1_out0), .D(Di), .count(LOW_carry), .Q(Ao[23:16]), .clk(or_2_out), .clr(or_1_out));  // open: carry
  Decoder #(.select(2), .disabled(0), .enable("false")) decoder_2 (
    .out0(A_2), .out1(B), .out2(C), .out3(D), .sel(DOR_q[1:0]));
  or or_4 (indicate, WRITE, READ);

  // Notes on the sheet:
  //   Dr: pull=down
  //   Di: pull=down
  //   A: pull=down
  //   param: pull=down
  //   IOR: pull=down
  //   RST: pull=down
  //   CLK: pull=down
  //   IOW: pull=down
  //   DOR
  //   0-1   drive select
  //   2      reset
  //   PORT 6
  //   PORT 7
  //   256 BYTES PER SECTOR
  //   0-2 bit    type for init size
  //   0h    no Storage
  //   1h    128 KB
  //   2h    512 KB
  //   * * *
  //   7h    16 MB
  //   3 bit    0 - RO / 1 - VOL
  //   4 bit    0 - fixed / 1 - removable
  //   5 bit    reserved
  //   6 bit    available
  //   7 bit    setup
  //   HIGH - first
  //   LOW - second
endmodule

module _16_MB_Storage__RO (
  input  WRITE,
  input  [7:0] Di,
  input  READ,
  input  [23:0] A,
  input  sel,
  output [7:0] Do,
  output [7:0] param
);

  wire [7:0] rom_1_data;

  ROM #(.addrWidth(24)) rom_1 (.addr(A), .data(rom_1_data), .sel(sel));
  assign Do = READ ? rom_1_data : 8'bz;  // Controlled_Buffer controlled_buffer_1
  assign param = sel ? 8'hc7 : 8'bz;  // Controlled_Buffer controlled_buffer_2

  // Notes on the sheet:
  //   READ: pull=down
  //   Di: pull=down
  //   WRITE: pull=down
  //   sel: pull=down
  //   A: pull=down
endmodule

module _16_MB_Storage__vol (
  input  [7:0] Di,
  input  [23:0] A,
  input  WRITE,
  input  READ,
  input  sel,
  output [7:0] Do,
  output [7:0] param
);

  wire [7:0] ram_1_data;

  assign Do = READ ? ram_1_data : 8'bz;  // Controlled_Buffer controlled_buffer_1
  RAM #(.addrWidth(24), .bus("separate")) ram_1 (
    .addr(A), .din(Di), .data(ram_1_data), .str(WRITE), .sel(sel), .clk(WRITE));  // open: ld, clr
  assign param = sel ? 8'hcf : 8'bz;  // Controlled_Buffer controlled_buffer_2

  // Notes on the sheet:
  //   READ: pull=down
  //   Di: pull=down
  //   sel: pull=down
  //   WRITE: pull=down
  //   A: pull=down
endmodule

module _128_KB_Storage__vol (
  input  [7:0] Di,
  input  READ,
  input  [23:0] A,
  input  WRITE,
  input  sel,
  output [7:0] Do,
  output [7:0] param
);

  wire [7:0] ram_1_data;

  RAM #(.addrWidth(17), .bus("separate")) ram_1 (
    .addr(A[16:0]), .din(Di), .data(ram_1_data), .str(WRITE), .sel(sel), .clk(WRITE));  // open: ld, clr
  assign Do = READ ? ram_1_data : 8'bz;  // Controlled_Buffer controlled_buffer_1
  assign param = sel ? 8'hc9 : 8'bz;  // Controlled_Buffer controlled_buffer_2

  // Notes on the sheet:
  //   A: pull=down
  //   READ: pull=down
  //   WRITE: pull=down
  //   sel: pull=down
  //   Di: pull=down
endmodule

module Removable_Storage_Drive (
  input  [7:0] DSi,
  input  [7:0] Di,
  input  READ,
  input  [23:0] A,
  input  WRITE,
  input  sel,
  input  [1:0] connI,
  output [7:0] DSo,
  output [16:0] Ao,
  output WE,
  output [7:0] Do,
  output indicate,
  output [7:0] param,
  output connO
);

  wire and_1_out;
  wire [8:0] counter_1_q;

  and and_1 (and_1_out, READ, sel);
  assign Ao = sel ? A[16:0] : 17'bz;  // Controlled_Buffer controlled_buffer_1
  and and_2 (WE, WRITE, sel);
  assign Do = and_1_out ? DSi : 8'bz;  // Controlled_Buffer controlled_buffer_2
  or or_1 (indicate, and_1_out, WE);
  Counter #(.width(9), .max('h1ff)) counter_1 (.Q(counter_1_q), .clk(and_1_out));  // open: load, D, count, carry, clr
  // Probe on counter_1_q
  assign param = sel ? {1'b1, connI[0], 2'b01, connI[1], 3'b001} : 8'bz;  // Controlled_Buffer controlled_buffer_3

  assign connO = 1'b1;
  assign DSo = Di;

  // Notes on the sheet:
  //   READ: pull=down
  //   sel: pull=down
  //   Di: pull=down
  //   WRITE: pull=down
  //   A: pull=down
  //   DSi: pull=down
  //   connI: pull=down
  //   ONLY 128 KB!!!
endmodule

module _128_KB_Removable_Storage_vol (
  input  [16:0] A,
  input  [7:0] Di,
  input  WE,
  input  connI,
  output [7:0] Do,
  output [1:0] connO
);

  RAM #(.addrWidth(17), .bus("separate")) ram_1 (
    .addr(A), .din(Di), .data(Do), .str(WE), .clk(WE));  // open: sel, ld, clr

  assign connO = {1'b1, connI};

  // Notes on the sheet:
  //   Di: pull=down
  //   connI: pull=down
  //   WE: pull=down
  //   VOL
endmodule

module _128_KB_Removable_Storage__RO (
  input  [16:0] A,
  input  [7:0] Di,
  input  WE,
  input  connI,
  output [7:0] Do,
  output [1:0] connO
);

  ROM #(.addrWidth(17)) rom_1 (.addr(A), .data(Do));  // open: sel

  assign connO = {1'b0, connI};

  // Notes on the sheet:
  //   WE: pull=down
  //   Di: pull=down
  //   connI: pull=down
  //   contents of rom_1 (hex, n*v repeats v):
  //   38 30 c 48 65 6c 6c 6f 2c 20 57 6f 72 6c 64 a 50 72 69 6e 74 65 64 20 66 72 6f 6d 20 72 65 6d 6f 76
  //   61 62 6c 65 20 73 74 6f 72 61 67 65 a 24 6 3 e 0 16 d 2e c 36 3 2a 4 6 3 e 1 2e c 36 10 2a 4 ff
  //   184*0 ab
  //   RO
endmodule

module display_variants (
);

  TTY #(.rows(5), .cols(20)) tty_1 ();  // open: data, clk, we, clr
  TTY #(.rows(5), .cols(20)) tty_2 ();  // open: data, clk, we, clr
  TTY #(.rows(5), .cols(20)) tty_3 ();  // open: data, clk, we, clr
  TTY #(.rows(5), .cols(20)) tty_4 ();  // open: data, clk, we, clr
  TTY #(.rows(5), .cols(20)) tty_5 ();  // open: data, clk, we, clr
  TTY #(.rows(5), .cols(20)) tty_6 ();  // open: data, clk, we, clr
  TTY #(.rows(5), .cols(20)) tty_7 ();  // open: data, clk, we, clr
  TTY #(.rows(5), .cols(20)) tty_8 ();  // open: data, clk, we, clr
endmodule
